// Logisim project ISA.circ as structural Verilog: 4 circuits, main circuit main
module main (
  input  [1:0] in_1
);

  wire Clk, WrMem;
  wire [2:0] undriven;
  wire [23:0] bit_extender_1_out, rom_1_data;
  wire [31:0] adder_2_out, bit_extender_2_out, multiplexer_1_out, multiplexer_2_out, multiplexer_3_out, PC_1,
       pc_1_pc_novo, ram_1_dout, registerbank_1_readdata1, registerbank_1_readdata2, ula_1_resultado;

  Multiplexer #(.select(2), .width(32)) multiplexer_1 (
    .in0(PC_1), .in1(adder_2_out), .out(multiplexer_1_out), .sel(in_1));  // open: in2, in3
  Clock clock_1 (.out(Clk));
  Adder #(.width(32)) adder_1 (.a(pc_1_pc_novo), .b(32'h1), .out(PC_1));  // open: cin, cout
  Adder #(.width(32)) adder_2 (.a(pc_1_pc_novo), .out(adder_2_out));  // open: b, cin, cout
  PC u_pc_1 (.Clk(Clk), .PC_Ant(multiplexer_1_out), .PC_Novo(pc_1_pc_novo));  // open: Reset
  Bit_Extender #(.in_width(32), .out_width(24), .\type ("input")) bit_extender_1 (
    .in(pc_1_pc_novo), .out(bit_extender_1_out));  // open: extend
  ROM #(.addrWidth(24), .dataWidth(24)) rom_1 (.addr(bit_extender_1_out), .data(rom_1_data));
  assign bit_extender_2_out = {{24{rom_1_data[23]}}, rom_1_data[23:16]};  // Bit_Extender bit_extender_2
  RegisterBank registerbank_1 (
    .WriteData(multiplexer_3_out), .RD(rom_1_data[15:12]), .Clk(Clk), .RS2(rom_1_data[11:8]),
    .RS1(rom_1_data[7:4]), .ReadData1(registerbank_1_readdata1), .ReadData2(registerbank_1_readdata2));  // open: WE
  Multiplexer #(.width(32)) multiplexer_2 (
    .in0(registerbank_1_readdata2), .in1(bit_extender_2_out), .out(multiplexer_2_out));  // open: sel
  Multiplexer #(.select(2), .width(32)) multiplexer_3 (
    .in0(ula_1_resultado), .in1(ram_1_dout), .in2(PC_1), .out(multiplexer_3_out));  // open: in3, sel
  ULA ula_1 (
    .Op2(multiplexer_2_out), .Op1(registerbank_1_readdata1), .Op_ULA(undriven), .Resultado(ula_1_resultado));  // open: zero, sinal
  RAM #(.addrWidth(24), .dataWidth(32)) ram_1 (
    .addr(ula_1_resultado[23:0]), .we(1'b1), .oe(WrMem), .clk(Clk), .din(registerbank_1_readdata2),
    .dout(ram_1_dout));
endmodule

module ULA (
  input  [31:0] Op2,
  input  [31:0] Op1,
  input  [2:0] Op_ULA,
  output zero,
  output sinal,
  output [31:0] Resultado
);

  wire [31:0] adder_1_out, and_1_out, negator_1_out, or_1_out, shifter_1_out, shifter_2_out,
       subtractor_1_out, xor_1_out;

  Adder #(.width(32)) adder_1 (.a(Op1), .b(Op2), .out(adder_1_out));  // open: cin, cout
  Subtractor #(.width(32)) subtractor_1 (.a(Op1), .b(Op2), .out(subtractor_1_out), .bout(sinal));  // open: bin
  assign and_1_out = Op1 & Op2;  // AND_Gate and_1, 32 bits wide
  assign or_1_out = Op1 | Op2;  // OR_Gate or_1, 32 bits wide
  assign xor_1_out = Op1 ^ Op2;  // XOR_Gate xor_1, 32 bits wide
  Shifter #(.width(32)) shifter_1 (.in(Op1), .\dist (Op2[4:0]), .out(shifter_1_out));
  Shifter #(.shift("lr"), .width(32)) shifter_2 (.in(Op1), .\dist (Op2[4:0]), .out(shifter_2_out));
  Negator #(.width(32)) negator_1 (.in(Op1), .out(negator_1_out));
  Multiplexer #(.select(3), .width(32)) multiplexer_1 (
    .in0(adder_1_out), .in1(subtractor_1_out), .in2(and_1_out), .in3(or_1_out), .in4(xor_1_out),
    .in5(shifter_1_out), .in6(shifter_2_out), .in7(negator_1_out), .out(Resultado), .sel(Op_ULA));
  nor nor_1 (zero, subtractor_1_out[0], subtractor_1_out[1], subtractor_1_out[2], subtractor_1_out[3], subtractor_1_out[4], subtractor_1_out[5], subtractor_1_out[6], subtractor_1_out[7], subtractor_1_out[8], subtractor_1_out[9], subtractor_1_out[10], subtractor_1_out[11], subtractor_1_out[12], subtractor_1_out[13], subtractor_1_out[14], subtractor_1_out[15], subtractor_1_out[16], subtractor_1_out[17], subtractor_1_out[18], subtractor_1_out[19], subtractor_1_out[20], subtractor_1_out[21], subtractor_1_out[22], subtractor_1_out[23], subtractor_1_out[24], subtractor_1_out[25], subtractor_1_out[26], subtractor_1_out[27], subtractor_1_out[28], subtractor_1_out[29], subtractor_1_out[30], subtractor_1_out[31]);

  // Other names for the same wires on the sheet: sgn = sinal
endmodule

module RegisterBank (
  input  [31:0] WriteData,
  input  [3:0] RS1,
  input  WE,
  input  [3:0] RD,
  input  [3:0] RS2,
  input  Clk,
  output [31:0] ReadData1,
  output [31:0] ReadData2
);

  wire demultiplexer_1_out1, demultiplexer_1_out2, demultiplexer_1_out3, demultiplexer_1_out4,
       demultiplexer_1_out5, demultiplexer_1_out6, demultiplexer_1_out7, demultiplexer_1_out8,
       demultiplexer_1_out9, demultiplexer_1_out10, demultiplexer_1_out11, demultiplexer_1_out12,
       demultiplexer_1_out13, demultiplexer_1_out14, demultiplexer_1_out15;
  wire [31:0] r1_q, r2_q, r3_q, r4_q, r5_q, r6_q, r7_q, r8_q, r9_q, r10_q, r11_q, r12_q, r13_q, r14_q, r15_q;

  Demultiplexer #(.select(4)) demultiplexer_1 (
    .out1(demultiplexer_1_out1), .out2(demultiplexer_1_out2), .out3(demultiplexer_1_out3),
    .out4(demultiplexer_1_out4), .out5(demultiplexer_1_out5), .out6(demultiplexer_1_out6),
    .out7(demultiplexer_1_out7), .out8(demultiplexer_1_out8), .out9(demultiplexer_1_out9),
    .out10(demultiplexer_1_out10), .out11(demultiplexer_1_out11), .out12(demultiplexer_1_out12),
    .out13(demultiplexer_1_out13), .out14(demultiplexer_1_out14), .out15(demultiplexer_1_out15), .in(WE),
    .sel(RD));  // open: out0
  Register #(.width(32)) r1 (.D(WriteData), .en(demultiplexer_1_out1), .clk(Clk), .Q(r1_q));  // open: clr
  Register #(.width(32)) r2 (.D(WriteData), .en(demultiplexer_1_out2), .clk(Clk), .Q(r2_q));  // open: clr
  Register #(.width(32)) r3 (.D(WriteData), .en(demultiplexer_1_out3), .clk(Clk), .Q(r3_q));  // open: clr
  Register #(.width(32)) r4 (.D(WriteData), .en(demultiplexer_1_out4), .clk(Clk), .Q(r4_q));  // open: clr
  Register #(.width(32)) r5 (.D(WriteData), .en(demultiplexer_1_out5), .clk(Clk), .Q(r5_q));  // open: clr
  Register #(.width(32)) r6 (.D(WriteData), .en(demultiplexer_1_out6), .clk(Clk), .Q(r6_q));  // open: clr
  Register #(.width(32)) r7 (.D(WriteData), .en(demultiplexer_1_out7), .clk(Clk), .Q(r7_q));  // open: clr
  Register #(.width(32)) r8 (.D(WriteData), .en(demultiplexer_1_out8), .clk(Clk), .Q(r8_q));  // open: clr
  Register #(.width(32)) r9 (.D(WriteData), .en(demultiplexer_1_out9), .clk(Clk), .Q(r9_q));  // open: clr
  Register #(.width(32)) r10 (.D(WriteData), .en(demultiplexer_1_out10), .clk(Clk), .Q(r10_q));  // open: clr
  Register #(.width(32)) r11 (.D(WriteData), .en(demultiplexer_1_out11), .clk(Clk), .Q(r11_q));  // open: clr
  Register #(.width(32)) r12 (.D(WriteData), .en(demultiplexer_1_out12), .clk(Clk), .Q(r12_q));  // open: clr
  Register #(.width(32)) r13 (.D(WriteData), .en(demultiplexer_1_out13), .clk(Clk), .Q(r13_q));  // open: clr
  Register #(.width(32)) r14 (.D(WriteData), .en(demultiplexer_1_out14), .clk(Clk), .Q(r14_q));  // open: clr
  Register #(.width(32)) r15 (.D(WriteData), .en(demultiplexer_1_out15), .clk(Clk), .Q(r15_q));  // open: clr
  Multiplexer #(.select(4), .width(32)) multiplexer_1 (
    .in0({32{1'b0}}), .in1(r1_q), .in2(r2_q), .in3(r3_q), .in4(r4_q), .in5(r5_q), .in6(r6_q), .in7(r7_q),
    .in8(r8_q), .in9(r9_q), .in10(r10_q), .in11(r11_q), .in12(r12_q), .in13(r13_q), .in14(r14_q),
    .in15(r15_q), .out(ReadData1), .sel(RS1));
  Multiplexer #(.select(4), .width(32)) multiplexer_2 (
    .in0({32{1'b0}}), .in1(r1_q), .in2(r2_q), .in3(r3_q), .in4(r4_q), .in5(r5_q), .in6(r6_q), .in7(r7_q),
    .in8(r8_q), .in9(r9_q), .in10(r10_q), .in11(r11_q), .in12(r12_q), .in13(r13_q), .in14(r14_q),
    .in15(r15_q), .out(ReadData2), .sel(RS2));

  // Notes on the sheet:
  //   r0
endmodule

module PC (
  input  [31:0] PC_Ant,
  input  Clk,
  input  Reset,
  output [31:0] PC_Novo
);

  Register #(.width(32)) register_1 (.D(PC_Ant), .en(1'b1), .clk(Clk), .Q(PC_Novo), .clr(Reset));
endmodule
